# Fritzing sketch circuit (saved by Fritzing 0.9.3b)

parts:
  LED1 = LED - 5mm [color="Green (555nm)" package="5 mm [THT]"]
  Part2 = Bluetooth HC-05 Macho
  S1 = Toggle Switch [package=THT]
  R2 = Resistor [tolerance=±5% resistance=22k package=THT]  # not connected
  R3 = Resistor [tolerance=±5% resistance=10k package=THT]
  Power_plug1 = Power plug
  J1 = Basic Servo
  S2 = Pushbutton [package=THT]
  Part1 = Arduino Uno (Rev3)
  R4 = Resistor [tolerance=±5% resistance=220 package=THT]  # not connected
  R5 = Resistor [tolerance=±5% resistance=10k package=THT]

nets:
  N1: LED1.cathode, Part1.GND, R5.Pin_0
  N2: Part2.TXD, Part1.D10_PWM/SS
  N3: Part2.RXD, R3.Pin_1
  N4: Part2.VCC, S1.L1
  N5: S1.L2, Part1.5V
  N6: R3.Pin_0, Part1.D11_PWM/MOSI
  GND: Power_plug1.GND, J1.gnd
  VCC: Power_plug1.VCC, J1.vcc
  N7: J1.pulse, Part1.D8
  N8: S2.leg1, Part1.D2
